# Fritzing sketch wiring (saved by Fritzing 0.9.4)
breadboards: 1

parts:
  part = Raspberry Pi Zero
  Pull_down = Resistor [tolerance=±5% resistance=47k package=THT]
  PC_817 = Sharp PC817 [package=THT]
  1N4148 = Diode [package=diode-1n4148]
  part_2 = Resistor [tolerance=±5% resistance=560 package=THT]
  Doorbell_12VAC = Inductor [package="400 mil [THT]"]  # not connected

nets:
  N1: part.pin_1, part.pin_17, PC_817.Pin_4
  N2: part.pin_6, part.pin_14, Pull_down.Pin_0
  N3: part.pin_16, Pull_down.Pin_1, PC_817.Pin_3
  N4: PC_817.Pin_1, 1N4148.C, part_2.Pin_1
